// Digital circuit adder.dig as structural Verilog
module adder (
  input  [15:0] ADD_instr,
  input  [15:0] ADDR_instr,
  input  [15:0] D_1,
  input  [15:0] D_2,
  output [23:0] add_merged
);

  wire [1:0] multiplexer_1_out_2;
  wire [15:0] add_1_s, add_2_s;
  wire [23:0] comparator_1_eq, multiplexer_1_out;
  wire [27:2] multiplexer_2_out;
  wire [43:4] multiplexer_1_out_3;

  Comparator #(.Bits(4)) comparator_1 (.a(ADD_instr[3:0]), .b(4'b0100), .eq(comparator_1_eq[0]));  // open: gt, lt
  Comparator #(.Bits(4)) comparator_2 (.a(ADDR_instr[3:0]), .b(4'b0101), .eq(multiplexer_1_out[0]));  // open: gt, lt
  Multiplexer #(.Bits(44)) multiplexer_1 (
    .sel(multiplexer_1_out[0]), .in_0({44{1'b0}}), .in_1({D_2, D_1, ADDR_instr[15:4]}),
    .out({multiplexer_1_out_3, multiplexer_1_out_2, multiplexer_1_out[4:3]}));
  Multiplexer #(.Bits(28)) multiplexer_2 (
    .sel(comparator_1_eq[0]), .in_0({28{1'b0}}), .in_1({D_1, ADD_instr[15:4]}),
    .out({multiplexer_2_out, comparator_1_eq[4:3]}));
  Add #(.Bits(16)) add_1 (
    .a(multiplexer_1_out_3[27:12]), .b(multiplexer_1_out_3[43:28]), .c_i(1'b0), .s(add_1_s),
    .c_o(multiplexer_1_out[23]));
  Add #(.Bits(16)) add_2 (
    .a({{6{1'b0}}, multiplexer_2_out[11:2]}), .b(multiplexer_2_out[27:12]), .c_i(1'b0), .s(add_2_s),
    .c_o(comparator_1_eq[23]));
  assign add_merged = {comparator_1_eq[23], add_2_s, 2'b00, comparator_1_eq[4:3], comparator_1_eq[4:3], comparator_1_eq[0]} | {multiplexer_1_out[23], add_1_s, multiplexer_1_out_2, multiplexer_1_out[4:3], multiplexer_1_out[4:3], multiplexer_1_out[0]};  // Or or_1, 24 bits wide
endmodule
