// Digital circuit alu.dig as structural Verilog
module alu (
  input  [15:0] D_1,
  input  [15:0] D_2,
  input  [15:0] ADD_instr,
  input  [15:0] ADDR_instr,
  output [1:0] rs_1,
  output [15:0] D_res,
  output [1:0] rd,
  output en,
  output [1:0] rs_2,
  output ovf
);

  wire [1:0] multiplexer_2_out;
  wire [11:0] multiplexer_1_out;
  wire [11:2] multiplexer_2_out_2;
  wire [15:0] add_1_s, add_2_s, multiplexer_1_out_2, multiplexer_2_out_3, multiplexer_2_out_4;
  wire [23:0] comparator_1_eq, comparator_2_eq;

  Comparator #(.Bits(4)) comparator_1 (.a(ADD_instr[3:0]), .b(4'b0100), .eq(comparator_1_eq[0]));  // open: gt, lt
  Multiplexer #(.Bits(28)) multiplexer_1 (
    .sel(comparator_1_eq[0]), .in_0({28{1'b0}}), .in_1({D_1, ADD_instr[15:4]}),
    .out({multiplexer_1_out_2, multiplexer_1_out}));
  Comparator #(.Bits(4)) comparator_2 (.a(ADDR_instr[3:0]), .b(4'b0101), .eq(comparator_2_eq[0]));  // open: gt, lt
  Multiplexer #(.Bits(44)) multiplexer_2 (
    .sel(comparator_2_eq[0]), .in_0({44{1'b0}}), .in_1({D_2, D_1, ADDR_instr[15:4]}),
    .out({multiplexer_2_out_4, multiplexer_2_out_3, multiplexer_2_out_2, multiplexer_2_out}));
  Add #(.Bits(16)) add_1 (
    .a(multiplexer_2_out_3), .b(multiplexer_2_out_4), .c_i(1'b0), .s(add_1_s), .c_o(comparator_2_eq[23]));
  Add #(.Bits(16)) add_2 (
    .a({{6{1'b0}}, multiplexer_1_out[11:2]}), .b(multiplexer_1_out_2), .c_i(1'b0), .s(add_2_s),
    .c_o(comparator_1_eq[23]));
  assign {ovf, D_res, rs_2, rs_1, rd, en} = {comparator_1_eq[23], add_2_s, 2'b00, multiplexer_1_out[1:0], multiplexer_1_out[1:0], comparator_1_eq[0]} | {comparator_2_eq[23], add_1_s, multiplexer_2_out_2[3:2], multiplexer_2_out, multiplexer_2_out, comparator_2_eq[0]};  // Or or_1, 24 bits wide
endmodule
