// Digital circuit cache.dig as structural Verilog
module cache (
  input  [15:0] LD_instr,
  input  [15:0] RAM_i,
  input  C,
  input  [15:0] ST_instr,
  input  [1:0] rs_1,
  input  [15:0] D_in,
  input  [1:0] rd,
  input  en,
  input  [1:0] rs_2,
  input  [15:0] MOV_instr,
  input  [1:0] rs_3,
  output [5:0] addr,
  output ld,
  output st,
  output [15:0] RAM_o,
  output [15:0] D_o1,
  output [15:0] D_o2,
  output [15:0] D_o3,
  output [15:0] D_o4
);

  wire decoder_1_out_0, ld_en, mov_en, multiplexer_7_out;
  wire [1:0] multiplexer_8_out, priorityencoder_1_num, priorityencoder_2_num, rd_t, rs_1_t, rs_store, st_rs4;
  wire [3:0] demultiplexer_2_out_0;
  wire [3:2] demultiplexer_2_out_1;
  wire [5:0] ld_addr, st_immaddr;
  wire [5:2] demultiplexer_1_out_1;
  wire [8:0] demultiplexer_3_out_0;
  wire [8:6] demultiplexer_3_out_1;
  wire [15:0] D_ld, D_reg;

  Demultiplexer #(.Bits(6)) demultiplexer_1 (
    .sel(ST_instr[4]), .in(ST_instr[10:5]), .out_0(st_immaddr), .out_1({demultiplexer_1_out_1, st_rs4}));
  Multiplexer #(.Bits(2)) multiplexer_1 (.sel(ST_instr[1]), .in_0(rs_1), .in_1(rs_store), .out(rs_1_t));
  Comparator #(.Bits(4)) comparator_1 (.a(MOV_instr[3:0]), .b(4'b0011), .eq(mov_en));  // open: gt, lt
  Comparator #(.Bits(4)) comparator_2 (.a(LD_instr[3:0]), .b(4'b0001), .eq(ld_en));  // open: gt, lt
  Decoder decoder_1 (.sel(LD_instr[6]), .out_0(decoder_1_out_0), .out_1(ld));
  // Probe on decoder_1_out_0
  Demultiplexer #(.Bits(4)) demultiplexer_2 (
    .sel(ST_instr[11]), .in(ST_instr[15:12]), .out_0(demultiplexer_2_out_0),
    .out_1({demultiplexer_2_out_1, rs_store}));
  Demultiplexer #(.Bits(9)) demultiplexer_3 (
    .sel(LD_instr[6]), .in(LD_instr[15:7]), .out_0(demultiplexer_3_out_0),
    .out_1({demultiplexer_3_out_1, ld_addr}));
  PriorityEncoder #(.Selector_Bits(2)) priorityencoder_1 (
    .in0(1'b1), .in1(en), .in2(mov_en), .in3(ld_en), .num(priorityencoder_1_num));  // open: any
  PriorityEncoder #(.Selector_Bits(2)) priorityencoder_2 (
    .in0(1'b1), .in1(ld), .in2(ST_instr[1]), .in3(ST_instr[4]), .num(priorityencoder_2_num));  // open: any
  Multiplexer #(.Selector_Bits(2), .Bits(16)) multiplexer_2 (
    .sel(priorityencoder_1_num), .in_0({16{1'b0}}), .in_1(D_in), .in_2(D_o4), .in_3(D_ld), .out(D_reg));
  Multiplexer #(.Bits(16)) multiplexer_3 (
    .sel(ST_instr[11]), .in_0({{12{1'b0}}, demultiplexer_2_out_0}), .in_1(D_o1), .out(RAM_o));
  Multiplexer #(.Bits(16)) multiplexer_4 (
    .sel(LD_instr[6]), .in_0({{7{1'b0}}, demultiplexer_3_out_0}), .in_1(RAM_i), .out(D_ld));
  Multiplexer #(.Selector_Bits(2), .Bits(6)) multiplexer_5 (
    .sel(priorityencoder_2_num), .in_0({6{1'b0}}), .in_1(ld_addr), .in_2(st_immaddr), .in_3(D_o4[5:0]),
    .out(addr));
  Multiplexer #(.Selector_Bits(2), .Bits(2)) multiplexer_6 (
    .sel(priorityencoder_1_num), .in_0(2'b00), .in_1(rd), .in_2(MOV_instr[5:4]), .in_3(LD_instr[5:4]),
    .out(rd_t));
  Multiplexer #(.Selector_Bits(2)) multiplexer_7 (
    .sel(priorityencoder_1_num), .in_0(1'b0), .in_1(en), .in_2(mov_en), .in_3(ld_en), .out(multiplexer_7_out));
  regfile regfile_1 (
    .en(multiplexer_7_out), .rd(rd_t), .D_i(D_reg), .C(C), .rs_1(rs_1_t), .rs_2(rs_2), .rs_3(rs_3),
    .rs_4(multiplexer_8_out), .D_o1(D_o1), .D_o2(D_o2), .D_o3(D_o3), .D_o4(D_o4));
  Multiplexer #(.Bits(2)) multiplexer_8 (.sel(mov_en), .in_0(st_rs4), .in_1(MOV_instr[7:6]), .out(multiplexer_8_out));

  assign st = ST_instr[1];

  // Other names for the same wires on the sheet: en_in = en; ld_rd[1:0] = LD_instr[5:4]; mov_rd[1:0] = MOV_instr[5:4];
  //   mov_rs4[1:0] = MOV_instr[7:6]; st_mode = ST_instr[4]; st_temp[5:0] = ST_instr[10:5]
endmodule
