// Digital circuit control.dig as structural Verilog
module control (
  input  [15:0] instr_in,
  input  [15:0] D_rs,
  input  C,
  output [1:0] rs,
  output [15:0] instr_o,
  output gt,
  output eq,
  output lt,
  output [5:0] A_new,
  output en
);

  wire comparator_1_eq, comparator_2_eq, comparator_3_eq, comparator_4_eq, comparator_5_eq, comparator_6_eq,
       comparator_6_gt, comparator_6_lt, multiplexer_6_out, multiplexer_7_out, multiplexer_8_out;
  wire [5:0] multiplexer_2_out, multiplexer_3_out, multiplexer_4_out, multiplexer_5_out;
  wire [15:0] CMP, demultiplexer_1_out_0, demultiplexer_1_out_1, demultiplexer_1_out_2,
       demultiplexer_1_out_3, demultiplexer_1_out_4, demultiplexer_1_out_5, demultiplexer_1_out_6,
       demultiplexer_1_out_7, demultiplexer_1_out_8, demultiplexer_1_out_9, demultiplexer_1_out_15, JEQ, JGT,
       JLT, JMP;

  Demultiplexer #(.Selector_Bits(4), .Bits(16)) demultiplexer_1 (
    .sel(instr_in[3:0]), .in(instr_in), .out_0(demultiplexer_1_out_0), .out_1(demultiplexer_1_out_1),
    .out_2(demultiplexer_1_out_2), .out_3(demultiplexer_1_out_3), .out_4(demultiplexer_1_out_4),
    .out_5(demultiplexer_1_out_5), .out_6(demultiplexer_1_out_6), .out_7(demultiplexer_1_out_7),
    .out_8(demultiplexer_1_out_8), .out_9(demultiplexer_1_out_9), .out_10(JMP), .out_11(JEQ), .out_12(JLT),
    .out_13(JGT), .out_14({CMP[15:6], rs, CMP[3:0]}), .out_15(demultiplexer_1_out_15));
  // Probe on instr_in[15:4]
  Multiplexer #(.Selector_Bits(4), .Bits(16)) multiplexer_1 (
    .sel(instr_in[3:0]), .in_0(demultiplexer_1_out_0), .in_1(demultiplexer_1_out_1),
    .in_2(demultiplexer_1_out_2), .in_3(demultiplexer_1_out_3), .in_4(demultiplexer_1_out_4),
    .in_5(demultiplexer_1_out_5), .in_6(demultiplexer_1_out_6), .in_7(demultiplexer_1_out_7),
    .in_8(demultiplexer_1_out_8), .in_9(demultiplexer_1_out_9), .in_10({16{1'b0}}), .in_11({16{1'b0}}),
    .in_12({16{1'b0}}), .in_13({16{1'b0}}), .in_14({16{1'b0}}), .in_15(demultiplexer_1_out_15), .out(instr_o));
  Comparator #(.Bits(4)) comparator_1 (.a(CMP[3:0]), .b(4'b1110), .eq(comparator_1_eq));  // open: gt, lt
  Comparator #(.Bits(4)) comparator_2 (.a(JMP[3:0]), .b(4'b1010), .eq(comparator_2_eq));  // open: gt, lt
  Multiplexer #(.Bits(6)) multiplexer_2 (
    .sel(comparator_2_eq), .in_0({6{1'b0}}), .in_1(JMP[9:4]), .out(multiplexer_2_out));
  Comparator #(.Bits(4)) comparator_3 (.a(JEQ[3:0]), .b(4'b1011), .eq(comparator_3_eq));  // open: gt, lt
  Multiplexer #(.Bits(6)) multiplexer_3 (
    .sel(comparator_3_eq), .in_0({6{1'b0}}), .in_1(JEQ[9:4]), .out(multiplexer_3_out));
  Comparator #(.Bits(4)) comparator_4 (.a(JLT[3:0]), .b(4'b1100), .eq(comparator_4_eq));  // open: gt, lt
  Multiplexer #(.Bits(6)) multiplexer_4 (
    .sel(comparator_4_eq), .in_0({6{1'b0}}), .in_1(JLT[9:4]), .out(multiplexer_4_out));
  Comparator #(.Bits(4)) comparator_5 (.a(JGT[3:0]), .b(4'b1101), .eq(comparator_5_eq));  // open: gt, lt
  Multiplexer #(.Bits(6)) multiplexer_5 (
    .sel(comparator_5_eq), .in_0({6{1'b0}}), .in_1(JGT[9:4]), .out(multiplexer_5_out));
  Comparator #(.Bits(16)) comparator_6 (
    .a(D_rs), .b({{6{1'b0}}, CMP[15:6]}), .gt(comparator_6_gt), .eq(comparator_6_eq), .lt(comparator_6_lt));
  Register register_1 (.D(comparator_6_gt), .C(C), .en(comparator_1_eq), .Q(gt));
  Register register_2 (.D(comparator_6_eq), .C(C), .en(comparator_1_eq), .Q(eq));
  Register register_3 (.D(comparator_6_lt), .C(C), .en(comparator_1_eq), .Q(lt));
  Multiplexer multiplexer_6 (.sel(eq), .in_0(1'b0), .in_1(comparator_3_eq), .out(multiplexer_6_out));
  Multiplexer multiplexer_7 (.sel(lt), .in_0(1'b0), .in_1(comparator_4_eq), .out(multiplexer_7_out));
  Multiplexer multiplexer_8 (.sel(gt), .in_0(1'b0), .in_1(comparator_5_eq), .out(multiplexer_8_out));
  Multiplexer #(.Selector_Bits(4)) multiplexer_9 (
    .sel(instr_in[3:0]), .in_0(1'b0), .in_1(1'b0), .in_2(1'b0), .in_3(1'b0), .in_4(1'b0), .in_5(1'b0),
    .in_6(1'b0), .in_7(1'b0), .in_8(1'b0), .in_9(1'b0), .in_10(comparator_2_eq), .in_11(multiplexer_6_out),
    .in_12(multiplexer_7_out), .in_13(multiplexer_8_out), .in_14(1'b0), .in_15(1'b0), .out(en));
  Multiplexer #(.Selector_Bits(4), .Bits(6)) multiplexer_10 (
    .sel(instr_in[3:0]), .in_0({6{1'b0}}), .in_1({6{1'b0}}), .in_2({6{1'b0}}), .in_3({6{1'b0}}),
    .in_4({6{1'b0}}), .in_5({6{1'b0}}), .in_6({6{1'b0}}), .in_7({6{1'b0}}), .in_8({6{1'b0}}),
    .in_9({6{1'b0}}), .in_10(multiplexer_2_out), .in_11(multiplexer_3_out), .in_12(multiplexer_4_out),
    .in_13(multiplexer_5_out), .in_14({6{1'b0}}), .in_15({6{1'b0}}), .out(A_new));

  // Other names for the same wires on the sheet: CMP[5:4] = rs; opcode[3:0] = instr_in[3:0]
endmodule
