// Digital circuit decoder.dig as structural Verilog
module decoder (
  input  [15:0] instr_i,
  input  C,
  output [15:0] NOP,
  output [15:0] LD,
  output [15:0] ST,
  output [15:0] INC,
  output [15:0] ADD,
  output [15:0] ADDR,
  output [15:0] SUB,
  output [15:0] SUBR,
  output [15:0] MUL,
  output [15:0] MULR,
  output [15:0] JMP,
  output [15:0] JEQ,
  output [15:0] JLT,
  output [15:0] JGT,
  output [15:0] HALT
);

  wire [15:0] register_1_q;

  Register #(.Bits(16)) register_1 (.D(instr_i), .C(C), .en(1'b1), .Q(register_1_q));
  Demultiplexer #(.Selector_Bits(4), .Bits(16)) demultiplexer_1 (
    .sel(register_1_q[3:0]), .in(register_1_q), .out_0(NOP), .out_1(LD), .out_2(ST), .out_3(INC),
    .out_4(ADD), .out_5(ADDR), .out_6(SUB), .out_7(SUBR), .out_8(MUL), .out_9(MULR), .out_10(JMP),
    .out_11(JEQ), .out_12(JLT), .out_13(JGT), .out_15(HALT));  // open: out_14
  // Probe on register_1_q[15:4]
endmodule
