// Digital circuit multiplier.dig as structural Verilog
module multiplier (
  input  [15:0] MUL_instr,
  input  [15:0] MULR_instr,
  input  [15:0] D_1,
  input  [15:0] D_2,
  output [23:0] mul_merged
);

  wire [1:0] multiplexer_1_out_2;
  wire [4:0] comparator_1_eq, multiplexer_1_out;
  wire [15:0] mul_1_mul, mul_2_mul;
  wire [27:2] multiplexer_2_out;
  wire [43:4] multiplexer_1_out_3;

  Comparator #(.Bits(4)) comparator_1 (.a(MUL_instr[3:0]), .b(4'b1000), .eq(comparator_1_eq[0]));  // open: gt, lt
  Comparator #(.Bits(4)) comparator_2 (.a(MULR_instr[3:0]), .b(4'b1001), .eq(multiplexer_1_out[0]));  // open: gt, lt
  Multiplexer #(.Bits(44)) multiplexer_1 (
    .sel(multiplexer_1_out[0]), .in_0({44{1'b0}}), .in_1({D_2, D_1, MULR_instr[15:4]}),
    .out({multiplexer_1_out_3, multiplexer_1_out_2, multiplexer_1_out[4:3]}));
  Multiplexer #(.Bits(28)) multiplexer_2 (
    .sel(comparator_1_eq[0]), .in_0({28{1'b0}}), .in_1({D_1, MUL_instr[15:4]}),
    .out({multiplexer_2_out, comparator_1_eq[4:3]}));
  Mul #(.Bits(8)) mul_1 (.a(multiplexer_1_out_3[19:12]), .b(multiplexer_1_out_3[35:28]), .mul(mul_1_mul));
  Mul #(.Bits(8)) mul_2 (.a(multiplexer_2_out[9:2]), .b(multiplexer_2_out[19:12]), .mul(mul_2_mul));
  assign mul_merged = {1'b0, mul_2_mul, 2'b00, comparator_1_eq[4:3], comparator_1_eq[4:3], comparator_1_eq[0]} | {1'b0, mul_1_mul, multiplexer_1_out_2, multiplexer_1_out[4:3], multiplexer_1_out[4:3], multiplexer_1_out[0]};  // Or or_1, 24 bits wide
endmodule
