// Digital circuit mux41.dig as structural Verilog
module mux41 (
  input  [3:0] I_0,
  input  [3:0] I_1,
  input  [3:0] I_2,
  input  [3:0] I_3,
  input  [1:0] sel,
  output [3:0] out
);

  wire not_1_out, not_2_out, not_3_out, not_4_out;
  wire [3:0] and_5_out, and_6_out, and_7_out, and_8_out;
  wire [3:3] and_1_out, and_2_out, and_3_out, and_4_out;

  and and_1 (and_1_out[3], not_1_out, not_2_out);
  not not_1 (not_1_out, sel[1]);
  not not_2 (not_2_out, sel[0]);
  not not_3 (not_3_out, sel[1]);
  not not_4 (not_4_out, sel[0]);
  and and_2 (and_2_out[3], not_3_out, sel[0]);
  and and_3 (and_3_out[3], sel[1], not_4_out);
  and and_4 (and_4_out[3], sel[1], sel[0]);
  assign and_5_out = I_0 & {4{and_1_out[3]}};  // And and_5, 4 bits wide
  assign and_6_out = I_1 & {4{and_2_out[3]}};  // And and_6, 4 bits wide
  assign and_7_out = I_2 & {4{and_3_out[3]}};  // And and_7, 4 bits wide
  assign and_8_out = I_3 & {4{and_4_out[3]}};  // And and_8, 4 bits wide
  assign out = and_5_out | and_6_out | and_7_out | and_8_out;  // Or or_1, 4 bits wide
endmodule
