// Digital circuit regfile.dig as structural Verilog
module regfile (
  input  en,
  input  [1:0] rd,
  input  [15:0] D_i,
  input  C,
  input  [1:0] rs_1,
  input  [1:0] rs_2,
  input  [1:0] rs_3,
  input  [1:0] rs_4,
  output [15:0] D_o1,
  output [15:0] D_o2,
  output [15:0] D_o3,
  output [15:0] D_o4
);

  wire demultiplexer_2_out_0, demultiplexer_2_out_1, demultiplexer_2_out_2, demultiplexer_2_out_3;
  wire [15:0] demultiplexer_1_out_0, demultiplexer_1_out_1, demultiplexer_1_out_2, demultiplexer_1_out_3,
       R0_q, R1_q, R2_q, R3_q;

  Demultiplexer #(.Selector_Bits(2), .Bits(16)) demultiplexer_1 (
    .sel(rd), .in(D_i), .out_0(demultiplexer_1_out_0), .out_1(demultiplexer_1_out_1),
    .out_2(demultiplexer_1_out_2), .out_3(demultiplexer_1_out_3));
  Demultiplexer #(.Selector_Bits(2)) demultiplexer_2 (
    .sel(rd), .in(en), .out_0(demultiplexer_2_out_0), .out_1(demultiplexer_2_out_1),
    .out_2(demultiplexer_2_out_2), .out_3(demultiplexer_2_out_3));
  Register #(.Bits(16)) R0 (.D(demultiplexer_1_out_0), .C(C), .en(demultiplexer_2_out_0), .Q(R0_q));
  Register #(.Bits(16)) R1 (.D(demultiplexer_1_out_1), .C(C), .en(demultiplexer_2_out_1), .Q(R1_q));
  Register #(.Bits(16)) R2 (.D(demultiplexer_1_out_2), .C(C), .en(demultiplexer_2_out_2), .Q(R2_q));
  Register #(.Bits(16)) R3 (.D(demultiplexer_1_out_3), .C(C), .en(demultiplexer_2_out_3), .Q(R3_q));
  Multiplexer #(.Selector_Bits(2), .Bits(16)) multiplexer_1 (
    .sel(rs_1), .in_0(R0_q), .in_1(R1_q), .in_2(R2_q), .in_3(R3_q), .out(D_o1));
  Multiplexer #(.Selector_Bits(2), .Bits(16)) multiplexer_2 (
    .sel(rs_2), .in_0(R0_q), .in_1(R1_q), .in_2(R2_q), .in_3(R3_q), .out(D_o2));
  Multiplexer #(.Selector_Bits(2), .Bits(16)) multiplexer_3 (
    .sel(rs_3), .in_0(R0_q), .in_1(R1_q), .in_2(R2_q), .in_3(R3_q), .out(D_o3));
  Multiplexer #(.Selector_Bits(2), .Bits(16)) multiplexer_4 (
    .sel(rs_4), .in_0(R0_q), .in_1(R1_q), .in_2(R1_q), .in_3(R3_q), .out(D_o4));
endmodule
