// Digital circuit subtractor.dig as structural Verilog
module subtractor (
  input  [15:0] SUB_instr,
  input  [15:0] SUBR_instr,
  input  [15:0] D_1,
  input  [15:0] D_2,
  output [23:0] sub_merged
);

  wire [1:0] multiplexer_1_out_2;
  wire [15:0] sub_1_s, sub_2_s;
  wire [23:0] comparator_1_eq, multiplexer_1_out;
  wire [27:2] multiplexer_2_out;
  wire [43:4] multiplexer_1_out_3;

  Comparator #(.Bits(4)) comparator_1 (.a(SUB_instr[3:0]), .b(4'b0110), .eq(comparator_1_eq[0]));  // open: gt, lt
  Comparator #(.Bits(4)) comparator_2 (.a(SUBR_instr[3:0]), .b(4'b0111), .eq(multiplexer_1_out[0]));  // open: gt, lt
  Multiplexer #(.Bits(44)) multiplexer_1 (
    .sel(multiplexer_1_out[0]), .in_0({44{1'b0}}), .in_1({D_2, D_1, SUBR_instr[15:4]}),
    .out({multiplexer_1_out_3, multiplexer_1_out_2, multiplexer_1_out[4:3]}));
  Multiplexer #(.Bits(28)) multiplexer_2 (
    .sel(comparator_1_eq[0]), .in_0({28{1'b0}}), .in_1({D_1, SUB_instr[15:4]}),
    .out({multiplexer_2_out, comparator_1_eq[4:3]}));
  Sub #(.Bits(16)) sub_1 (
    .a(multiplexer_1_out_3[27:12]), .b(multiplexer_1_out_3[43:28]), .c_i(1'b0), .s(sub_1_s),
    .c_o(multiplexer_1_out[23]));
  Sub #(.Bits(16)) sub_2 (
    .a(multiplexer_2_out[27:12]), .b({{6{1'b0}}, multiplexer_2_out[11:2]}), .c_i(1'b0), .s(sub_2_s),
    .c_o(comparator_1_eq[23]));
  assign sub_merged = {comparator_1_eq[23], sub_2_s, 2'b00, comparator_1_eq[4:3], comparator_1_eq[4:3], comparator_1_eq[0]} | {multiplexer_1_out[23], sub_1_s, multiplexer_1_out_2, multiplexer_1_out[4:3], multiplexer_1_out[4:3], multiplexer_1_out[0]};  // Or or_1, 24 bits wide
endmodule
